# Fritzing sketch 3.3_Zumbador (saved by Fritzing 0.9.3b)
breadboards: 1

parts:
  part = Arduino Uno (Rev3)
  part_2 = Piezo Speaker

nets:
  N1: part.GND, part_2.pin1
  N2: part.D6_PWM, part_2.pin2
