# Fritzing sketch Led (saved by Fritzing 0.9.3b)
breadboards: 1

parts:
  part = Arduino Uno (Rev3)
  R1 = Resistor [tolerance=±5% resistance=220 package=THT]
  LED1 = LED - 5mm [color="Red (633nm)" package="5 mm [THT]"]

nets:
  N1: part.GND, LED1.cathode
  N2: part.D5_PWM, R1.Pin_1
  N3: R1.Pin_0, LED1.anode
