# Fritzing sketch Pulsador (saved by Fritzing 0.9.2b)
breadboards: 1

parts:
  S1 = Pushbutton [package="[THT]"]
  R1 = Resistor [tolerance=±5% resistance=10k package=THT]
  Parte1 = Arduino Uno (Rev3)

nets:
  N1: S1.Pin_1, S1.Pin_2, R1.Pin_0, Parte1.D2
  N2: S1.Pin_3, S1.Pin_4, Parte1.5V
  N3: R1.Pin_1, Parte1.GND
