# Fritzing sketch 4-3 Pulsador Zumbador (saved by Fritzing 0.9.2b)
breadboards: 1

parts:
  Parte1 = Arduino Uno (Rev3)
  S1 = Pushbutton [package="[THT]"]
  R1 = Resistor [tolerance=±5% resistance=10k package=THT]
  J1 = Piezo Speaker

nets:
  N1: Parte1.D12/MISO, J1.pin2
  N2: Parte1.GND, R1.Pin_0, J1.pin1
  N3: Parte1.D2, S1.Pin_1, S1.Pin_2, R1.Pin_1
  N4: Parte1.5V, S1.Pin_3, S1.Pin_4
