# Fritzing sketch LDR (saved by Fritzing 0.9.3b)
breadboards: 1

parts:
  part = Arduino Uno (Rev3)
  R2 = Resistor [tolerance=±5% resistance=10k package=THT]
  R3 = Photocell (LDR) [package=THT]

nets:
  N1: part.A0, R2.Pin_1, R3.pin_0
  N2: part.GND, R2.Pin_0
  N3: part.5V, R3.pin_1
