# Fritzing sketch RGB_Catodo_comun (saved by Fritzing 0.9.3b)
breadboards: 1

parts:
  part = Resistor [tolerance=±5% resistance=220 package=THT]
  part_2 = RGB LED (com. cathode, rgb) [package="5 mm [THT]"]
  part_3 = Arduino Uno (Rev3)
  part_4 = Resistor [tolerance=±5% resistance=220 package=THT]
  part_5 = Resistor [tolerance=±5% resistance=220 package=THT]

nets:
  N1: part.Pin_0, part_3.D11_PWM/MOSI
  N2: part.Pin_1, part_2.red_anode
  N3: part_2.common_cathode, part_3.GND
  N4: part_2.green_anode, part_4.Pin_1
  N5: part_2.blue_anode, part_5.Pin_1
  N6: part_3.D9_PWM, part_5.Pin_0
  N7: part_3.D10_PWM/SS, part_4.Pin_0
