# Fritzing sketch Indicador_Temperaturac_LED_RGB (saved by Fritzing 0.9.3b)
breadboards: 1

parts:
  Componente1 = Arduino Uno (Rev3)
  LED1 = RGB LED (com. cathode, rgb) [package="5 mm [THT]"]
  U1 = TMP36 [package=to-92-kit]
  R1 = Resistor [tolerance=±5% resistance=220 package=THT]
  R2 = Resistor [tolerance=±5% resistance=220 package=THT]
  R3 = Resistor [tolerance=±5% resistance=220 package=THT]

nets:
  N1: Componente1.A0, U1.VOUT
  N2: Componente1.D9_PWM, R1.Pin_0
  N3: Componente1.D10_PWM/SS, R3.Pin_0
  N4: Componente1.D11_PWM/MOSI, R2.Pin_0
  5V: Componente1.5V, U1.VCC
  GND: Componente1.GND, LED1.common_cathode, U1.GND
  N5: LED1.red_anode, R1.Pin_1
  N6: LED1.green_anode, R3.Pin_1
  N7: LED1.blue_anode, R2.Pin_1

custom parts:
  RGB LED (com. cathode, rgb): A 5mm tri-color LED with red, green and blue inside.
