# Fritzing sketch servo2 (saved by Fritzing 0.9.2b)
breadboards: 1

parts:
  U1 = Arduino Uno (Rev3)
  J1 = Basic Servo
  C1 = Electrolytic Capacitor [capacitance=470µF package="100 mil [THT, electrolytic]"]

nets:
  N1: U1.D8, J1.pulse
  GND: U1.GND, J1.gnd, C1.-
  5V: U1.5V, J1.vcc, C1.+
