# Fritzing sketch servoPot (saved by Fritzing 0.9.2b)
breadboards: 1

parts:
  U1 = Arduino Uno (Rev3)
  J1 = Basic Servo
  R1 = Rotary Potentiometer (Small) [maximum_resistance=10kΩ package=THT]

nets:
  N1: U1.A0, R1.wiper
  N2: U1.D8, J1.pulse
  GND: U1.GND, J1.gnd, R1.leg1
  5V: U1.5V, J1.vcc, R1.leg2
