# Fritzing sketch Control_Motor_CC_L298 (saved by Fritzing 0.9.3b)

parts:
  Componente1 = Arduino Uno (Rev3)
  M1 = DC Motor
  J3 = Power Jack [package=power_jack_smd]
  S1 = H-Bridge with L298N

nets:
  N1: Componente1.D8, S1.IN4
  N2: Componente1.D9_PWM, S1.IN3
  GND: Componente1.GND, J3.GND, S1.GND
  N3: Componente1.D6_PWM, S1.ENB
  N4: M1.pin_1, S1.M2-02
  N5: M1.pin_2, S1.M2-01
  N6: J3.GNDBREAK, S1.12V
  N7: S1.ENA, S1.ENA-5V

custom parts:
  H-Bridge with L298N: h-bridge
