# Fritzing sketch 9.1_Temperatura_LCD_I2C (saved by Fritzing 0.9.3b)
breadboards: 1

parts:
  part = Arduino Uno (Rev3)
  part_2 = TMP36 [package=to-92-kit]
  part_3 = LCD1602-I2C

nets:
  N1: part.A0, part_2.VOUT
  GND: part.GND, part_2.GND, part_3.GND
  N2: part.A4/SDA, part_3.SDA
  N3: part.A5/SCL, part_3.SCL
  VCC: part.5V, part_2.VCC, part_3.VCC

custom parts:
  LCD1602-I2C: A standard character display, usually with 2x16 characters. Comes in many colors with LCM1602 IIC attached.
