# Fritzing sketch Temperatura_LCD_I2C (saved by Fritzing 0.9.3b)
breadboards: 1

parts:
  Componente1 = Arduino Uno (Rev3)
  U1 = TMP36 [package=to-92-kit]
  Componente2 = LCD1602-I2C

nets:
  N1: Componente1.A0, U1.VOUT
  GND: Componente1.GND, U1.GND, Componente2.GND
  N2: Componente1.A4/SDA, Componente2.SDA
  N3: Componente1.A5/SCL, Componente2.SCL
  VCC: Componente1.5V, U1.VCC, Componente2.VCC

custom parts:
  LCD1602-I2C: A standard character display, usually with 2x16 characters. Comes in many colors with LCM1602 IIC attached.
