# Fritzing sketch Display-7-1 (saved by Fritzing 0.9.2b)
breadboards: 1

parts:
  DI1 = 7-Segment LED Display [package=THT]
  U1 = 74HC595 SMD [package="SO16 [SMD]"]
  R1 = Resistor [tolerance=±5% resistance=1k package=THT]
  R2 = Resistor [tolerance=±5% resistance=1k package=THT]
  R3 = Resistor [tolerance=±5% resistance=1k package=THT]
  R4 = Resistor [tolerance=±5% resistance=1k package=THT]
  R5 = Resistor [tolerance=±5% resistance=1k package=THT]
  R6 = Resistor [tolerance=±5% resistance=1k package=THT]
  R7 = Resistor [tolerance=±5% resistance=1k package=THT]
  R8 = Resistor [tolerance=±5% resistance=1k package=THT]
  Parte1 = Arduino Uno (Rev3)

nets:
  N1: DI1.cathodeE, R8.Pin_1
  N2: DI1.cathodeD, R7.Pin_1
  VCC: DI1.commAnode#2, U1.MR, U1.VCC, Parte1.5V
  N3: DI1.cathodeC, R6.Pin_0
  N4: DI1.cathodeDP, R5.Pin_0
  N5: DI1.cathodeB, R1.Pin_0
  N6: DI1.cathodeA, R2.Pin_0
  N7: DI1.cathodeF, R4.Pin_1
  N8: DI1.cathodeG, R3.Pin_1
  N9: U1.Q1, R1.Pin_1
  N10: U1.Q2, R6.Pin_1
  N11: U1.Q3, R7.Pin_0
  N12: U1.Q4, R8.Pin_0
  N13: U1.Q5, R4.Pin_0
  N14: U1.Q6, R3.Pin_0
  N15: U1.Q7, R5.Pin_1
  GND: U1.GND, U1.OE, Parte1.GND
  N16: U1.SH_CP, Parte1.D12/MISO
  N17: U1.ST_CP, Parte1.D11_PWM/MOSI
  N18: U1.DS, Parte1.D10_PWM/SS
  N19: U1.Q0, R2.Pin_1
