# Fritzing sketch ControlLedPWM (saved by Fritzing 0.9.3b)

parts:
  part = Arduino Uno (Rev3)
  R1 = Resistor [tolerance=±5% resistance=220 package=THT]
  LED1 = LED - 5mm [color="Red (633nm)" package="5 mm [THT]"]

nets:
  N1: part.D9_PWM, R1.Pin_1
  N2: part.GND, LED1.cathode
  N3: R1.Pin_0, LED1.anode
