# Fritzing sketch Bluetooth-LED (saved by Fritzing 0.9.2b)

parts:
  Parte2 = Arduino Uno (Rev3)
  Parte4 = Bluetooth HC-06
  LED1 = LED - 5mm [color="Red (633nm)" package="5 mm [THT]"]

nets:
  N1: Parte2.D13/SCK, LED1.anode
  GND: Parte2.GND, Parte4.GND, LED1.cathode
  N2: Parte2.D0/RX, Parte4.TXD
  N3: Parte2.D1/TX, Parte4.RXD
  5V: Parte2.5V, Parte4.VCC
