# Fritzing sketch Hall (saved by Fritzing 0.9.3b)
breadboards: 1

parts:
  R1 = Resistor [tolerance=±5% resistance=10k package=THT]
  part = Arduino Uno (Rev3)
  Q1 = PNP-Transistor [package="TO92 [THT]"]

nets:
  N1: R1.Pin_0, part.D5_PWM, Q1.C
  N2: R1.Pin_1, part.5V, Q1.E
  N3: part.GND, Q1.B
