# Fritzing sketch Tilt (saved by Fritzing 0.9.3b)
circuit board: 6.88566cm x 5.36311cm
breadboards: 1

parts:
  Switch = Tilt Switch [package=THT]
  Arduino1 = Arduino Uno (Rev3)
  R1 = Resistor [tolerance=±5% resistance=100k package=THT]

nets:
  N1: Switch.Pin_1, Arduino1.D2, R1.Pin_1
  N2: Switch.Pin_2, Arduino1.5V
  N3: Arduino1.GND, R1.Pin_0

// code stored in the sketch: _7.2.1_-_Boton.ino

#define PIN_TILT   2
#define PIN_LED   13

void setup() {
  pinMode(PIN_BOTON, INPUT);
  pinMode(PIN_LED,OUTPUT);
}


void loop() {
  int iEstadoBoton=digitalRead(PIN_BOTON);

  digitalWrite(PIN_LED,iEstadoBoton);

  delay(10);
}
Codig
