# Fritzing sketch Pulsador-LED (saved by Fritzing 0.9.2b)
breadboards: 1

parts:
  S1 = Pushbutton [package="[THT]"]
  LED1 = LED - 5mm [color="White (4500K)" package="5 mm [THT]"]
  R2 = Resistor [tolerance=±5% resistance=220 package=THT]
  R1 = Resistor [tolerance=±5% resistance=10k package=THT]
  U1 = Arduino Uno (Rev3)

nets:
  N1: S1.Pin_1, S1.Pin_2, R1.Pin_0, U1.D2
  N2: S1.Pin_3, S1.Pin_4, U1.5V
  N3: LED1.cathode, R2.Pin_0
  N4: LED1.anode, U1.D12/MISO
  N5: R2.Pin_1, R1.Pin_1, U1.GND
