# Fritzing sketch Potenciometro (saved by Fritzing 0.9.3b)
breadboards: 1

parts:
  part = Arduino Uno (Rev3)
  R1 = Rotary Potentiometer (Small) [maximum_resistance=100kΩ package=THT]

nets:
  N1: part.A0, R1.wiper
  N2: part.5V, R1.leg2
  N3: part.GND, R1.leg1
