# Fritzing sketch accelerometro-mma7361 (saved by Fritzing 0.9.3b)

parts:
  part = Arduino Uno (Rev3)
  U1 = MMA7361 [package=lga14]
  R1 = Resistor [tolerance=±5% resistance=10k package=THT]

nets:
  N1: part.A0, U1.ZOUT
  N2: part.A1, U1.YOUT
  N3: part.A2, U1.XOUT
  N4: part.GND, U1.GSELECT, U1.G
  3V3: part.3V3, U1.VDD, R1.Pin_1
  5V: part.5V, U1.VSS
  N5: U1.SLEEP, R1.Pin_0

custom parts:
  MMA7361: 3-axis 1.5/6g analog output accelerometer
