# Fritzing sketch Piezo (saved by Fritzing 0.9.3b)
breadboards: 1

parts:
  part = Arduino Uno (Rev3)
  R1 = Resistor [tolerance=±5% resistance=1M package=THT]
  part_2 = Piezo Speaker

nets:
  N1: part.A0, R1.Pin_0, part_2.pin2
  N2: part.GND, R1.Pin_1, part_2.pin1
