# Fritzing sketch TMP36 (saved by Fritzing 0.9.3b)
breadboards: 1

parts:
  part = Arduino Uno (Rev3)
  part_2 = TMP36 [package=to-92-kit]

nets:
  N1: part.A0, part_2.VOUT
  GND: part.GND, part_2.GND
  5V: part.5V, part_2.VCC
