# Fritzing sketch LDR-LED (saved by Fritzing 0.9.2b)
breadboards: 1

parts:
  Parte1 = Arduino Uno (Rev3)
  R1-LDR = Photocell (LDR) [package=THT]
  R2 = Resistor [tolerance=±5% resistance=10k package=THT]
  LED1 = LED - 5mm [color="Red (633nm)" package="5 mm [THT]"]
  R3 = Resistor [tolerance=±5% resistance=220 package=THT]

nets:
  N1: Parte1.A0, R1-LDR.pin_1, R2.Pin_0
  N2: Parte1.D12/MISO, LED1.anode
  N3: Parte1.GND, R2.Pin_1, R3.Pin_1
  N4: Parte1.5V, R1-LDR.pin_0
  N5: LED1.cathode, R3.Pin_0
