# Fritzing sketch Termostato (saved by Fritzing 0.9.3b)
breadboards: 1

parts:
  part = Arduino Uno (Rev3)
  part_2 = TMP36 [package=to-92-kit]
  part_3 = Rotary Potentiometer (Small) [maximum_resistance=10kΩ package=THT]
  LED1 = LED - 5mm [color="Green (570nm)" package="5 mm [THT]"]
  part_4 = Resistor [tolerance=±5% resistance=220 package=THT]

nets:
  N1: part.A0, part_2.VOUT
  N2: part.A3, part_3.wiper
  GND: part.GND, part_2.GND, part_3.leg2, part_4.Pin_0
  N3: part.D6_PWM, LED1.anode
  5V: part.5V, part_2.VCC, part_3.leg1
  N4: LED1.cathode, part_4.Pin_1
