# Fritzing sketch RGB_Anodo_comun (saved by Fritzing 0.9.3b)
breadboards: 1

parts:
  R1 = Resistor [tolerance=±5% resistance=220 package=THT]
  Componente1 = Arduino Uno (Rev3)
  R2 = Resistor [tolerance=±5% resistance=220 package=THT]
  R3 = Resistor [tolerance=±5% resistance=220 package=THT]
  LED1 = RGB LED - (4 legs) [package="5 mm [THT]"]

nets:
  N1: R1.Pin_0, Componente1.D9_PWM
  N2: R1.Pin_1, LED1.blue_cathode
  N3: Componente1.D10_PWM/SS, R2.Pin_0
  N4: Componente1.D11_PWM/MOSI, R3.Pin_0
  N5: Componente1.5V, LED1.common_anode
  N6: R2.Pin_1, LED1.green_cathode
  N7: R3.Pin_1, LED1.red_cathode
