# Fritzing sketch 6-4 PIR-LED (saved by Fritzing 0.9.2b)
breadboards: 1

parts:
  R1 = Resistor [tolerance=±5% resistance=220 package=THT]
  LED = LED - 5mm [color="White (4500K)" package="5 mm [THT]"]
  PIR1 = PIR sensor
  Parte1 = Arduino Uno (Rev3)

nets:
  N1: R1.Pin_0, LED.cathode
  GND: R1.Pin_1, PIR1.GND, Parte1.GND
  N2: LED.anode, Parte1.D12/MISO
  VDD: PIR1.VDD, Parte1.5V
  N3: PIR1.SIG, Parte1.D3_PWM
