# Fritzing sketch SensorDistancia (saved by Fritzing 0.9.2b)

parts:
  Parte1 = SRF05 Ultrasonic Rangefinder
  Parte2 = Arduino Uno (Rev3)

nets:
  VCC: Parte1.VCC, Parte2.5V
  N1: Parte1.Trig, Parte2.D11_PWM/MOSI
  N2: Parte1.Echo, Parte2.D10_PWM/SS
  GND: Parte1.GND, Parte2.GND
